// Logisim project DD_DESIGN_ASSIGNMENT.circ as structural Verilog: 1 circuit, main circuit main
module main (
  input  Night_Senso__Real_Time_Clock,
  input  [2:0] Light_Sensor,
  input  Engine,
  input  Automated_headlights_switch,
  input  Incoming_Car,
  input  [1:0] Manual_Control,
  input  Adaptive,
  input  L_prime_R,
  input  Fog_Light_Switch,
  output out_10,
  output [1:0] Headlight,
  output [1:0] Adaptive_lights,
  output Fog_Lights
);

  wire and_1_out, and_4_out, and_5_out, and_6_out, and_7_out, and_8_out, and_9_out, and_10_out, and_11_out,
       and_12_out, and_13_out, clock_1_out, decoder_1_out0, decoder_1_out1, decoder_1_out2, decoder_1_out3,
       decoder_1_out4, decoder_1_out5, decoder_1_out6, decoder_1_out7, decoder_2_out0, decoder_2_out1,
       decoder_2_out2, j_k_ff_1_qn, j_k_ff_2_q, not_1_out, not_2_out, not_3_out, not_4_out, not_5_out,
       not_6_out, not_7_out, or_1_out, or_2_out, or_3_out, or_4_out, or_5_out, or_6_out, or_7_out, or_8_out,
       or_9_out, or_10_out, or_11_out, xor_1_out, xor_2_out, xor_3_out;

  Decoder #(.select(3)) decoder_1 (
    .out0(decoder_1_out0), .out1(decoder_1_out1), .out2(decoder_1_out2), .out3(decoder_1_out3),
    .out4(decoder_1_out4), .out5(decoder_1_out5), .out6(decoder_1_out6), .out7(decoder_1_out7),
    .sel(Light_Sensor));  // open: en
  not not_1 (not_1_out, Automated_headlights_switch);
  Decoder #(.select(2)) decoder_2 (
    .out0(decoder_2_out0), .out1(decoder_2_out1), .out2(decoder_2_out2), .sel(Manual_Control), .en(not_1_out));  // open: out3
  or or_1 (or_1_out, decoder_1_out0, decoder_1_out1);
  or or_2 (or_2_out, decoder_1_out2, decoder_1_out3, decoder_1_out4);
  or or_3 (or_3_out, decoder_1_out5, decoder_1_out6, decoder_1_out7);
  and and_1 (and_1_out, Engine, Automated_headlights_switch);
  and and_2 (Adaptive_lights[0], Adaptive, L_prime_R);
  and and_3 (Adaptive_lights[1], Adaptive, not_2_out);
  not not_2 (not_2_out, L_prime_R);
  and and_4 (and_4_out, and_1_out, or_1_out);
  and and_5 (and_5_out, and_1_out, or_2_out);
  and and_6 (and_6_out, and_1_out, or_3_out);
  not not_3 (not_3_out, Engine);
  and and_7 (and_7_out, and_4_out, Incoming_Car);
  and and_8 (and_8_out, not_3_out, Automated_headlights_switch);
  and and_9 (and_9_out, Night_Senso__Real_Time_Clock, or_4_out);
  or or_4 (or_4_out, and_8_out, and_6_out);
  xor xor_1 (xor_1_out, and_7_out, and_4_out);
  or or_5 (or_5_out, and_7_out, and_9_out);
  xor xor_2 (xor_2_out, or_5_out, and_5_out);
  xor xor_3 (xor_3_out, and_9_out, or_4_out);
  or or_6 (or_6_out, decoder_2_out0, xor_3_out);
  or or_7 (or_7_out, decoder_2_out1, xor_2_out);
  or or_8 (or_8_out, decoder_2_out2, xor_1_out);
  or or_9 (or_9_out, or_3_out, not_4_out);
  not not_4 (not_4_out, Engine);
  or or_10 (or_10_out, decoder_2_out2, decoder_2_out1);
  Priority_Encoder #(.select(2)) priority_encoder_1 (
    .in0(or_6_out), .in1(or_7_out), .in2(or_8_out), .out(Headlight));  // open: in3, gs, en_out, en_in
  and and_10 (and_10_out, not_5_out, not_6_out);
  _7_Segment_Display u_7_segment_display_1 (
    .g(and_12_out), .f(and_10_out), .a(not_6_out), .b(1'b1), .e(not_6_out), .d(not_6_out), .c(not_5_out),
    .dp(Fog_Light_Switch));
  and and_11 (and_11_out, or_9_out, or_10_out, not_1_out);
  not not_5 (not_5_out, Headlight[1]);
  not not_6 (not_6_out, Headlight[0]);
  and and_12 (and_12_out, Headlight[1], not_6_out);
  or or_11 (or_11_out, j_k_ff_2_q, not_7_out);
  not not_7 (not_7_out, and_11_out);
  and and_13 (and_13_out, j_k_ff_1_qn, and_11_out);
  Clock clock_1 (.out(clock_1_out));
  J_K_Flip_Flop j_k_ff_1 (
    .J(j_k_ff_2_q), .clk(clock_1_out), .K(or_11_out), .Qn(j_k_ff_1_qn));  // open: Q, preset, en, reset
  J_K_Flip_Flop j_k_ff_2 (.J(and_13_out), .clk(clock_1_out), .K(1'b1), .Q(j_k_ff_2_q));  // open: Qn, preset, en, reset
  and and_14 (out_10, j_k_ff_2_q, j_k_ff_1_qn);

  assign Fog_Lights = Fog_Light_Switch;
endmodule
